// Logisim project video_card.circ as structural Verilog: 3 circuits, main circuit Graphic_ROM
module Graphic_ROM (
  input  [3:0] char_pix_pos,
  input  [6:0] char_code,
  output [7:0] ROM_data
);

  // Probe on {1'b0, char_code, char_pix_pos}
  ROM #(.addrWidth(12)) rom_1 (.addr({1'b0, char_code, char_pix_pos}), .data(ROM_data));
  // Probe on ROM_data

  // Notes on the sheet:
  //   contents of rom_1 (hex, n*v repeats v):
  //   768*0 e 11 13 15 19 11 11 e 8*0 4 c 14 5*4 8*0 1f 1 1 1f 10 10 10 1f 8*0 1f 1 1 1e 1 1 1 1f 8*0 2 6
  //   a 12 1f 2 2 2 8*0 1f 10 10 1e 1 1 1 1e 8*0 f 10 10 1e 11 11 11 e 8*0 1f 1 2 5*4 8*0 e 11 11 11 e 11
  //   11 e 8*0 e 11 11 11 f 1 1 e 120*0 1f 11 11 11 1f 11 11 11 8*0 1f 11 11 1e 12 11 11 1f 8*0 1f 6*10 1f
  //   8*0 1c 12 4*11 12 1c 8*0 1f 10 10 1f 10 10 10 1f 8*0 1f 10 10 1f 4*10 8*0 1f 10 10 17 11 11 11 1f
  //   8*0 11 11 11 1f 4*11 8*0 1f 6*4 1f 8*0 1f 6*4 1c 8*0 11 12 14 18 14 12 11 11 8*0 7*10 1f 8*0 11 1b
  //   15 5*11 8*0 11 1a 19 15 15 13 13 11 8*0 1f 6*11 1f 8*0 1f 11 11 1f 4*10 8*0 1f 11 11 11 15 13 1e 1
  //   8*0 1f 11 11 1e 12 11 11 11 8*0 1f 10 10 1f 1 1 1 1f 8*0 1f 7*4 8*0 7*11 1f 8*0 6*11 a 4 8*0 4*11 15
  //   15 15 1f 8*0 11 a 4*4 a 11 8*0 11 11 11 1f 1 1 1 1f 8*0 1f 1 2 4 4 8 10 1f
endmodule

module Graphic_ctrl (
  input  [4:0] rom_data,
  input  [4:0] x,
  input  [2:0] y,
  input  EN,
  input  clk,
  input  cursor,
  input  \continue ,
  output WE,
  output [5:0] dy,
  output [6:0] dx,
  output [3:0] color,
  output stopped,
  output [3:0] pix_po
);

  wire and_1_out, and_2_out, and_3_out, clk_t, counter_2_carry, multiplexer_1_out, not_1_out,
       pull_resistor_3_node, y_inc;
  wire [2:0] register_2_q, w_sel;
  wire [4:0] register_1_q;
  wire [5:0] y_t;
  wire [6:0] x_t;

  Pull_Resistor #(.pull(1)) pull_resistor_1 (.node(color));
  and and_1 (and_1_out, EN, clk);
  or or_1 (clk_t, and_1_out, cursor);
  Counter #(.max('h4), .width(3)) counter_1 (
    .clr(stopped), .up(1'b1), .count(1'b1), .clk(clk_t), .carry(y_inc), .Q(w_sel));  // open: load, D
  and and_2 (and_2_out, clk_t, cursor);
  // Probe on w_sel
  Register #(.width(5)) register_1 (.D(x), .en(1'b1), .clk(and_2_out), .Q(register_1_q));  // open: clr
  Register #(.width(3)) register_2 (.D(y), .en(1'b1), .clk(and_2_out), .Q(register_2_q));  // open: clr
  Counter #(.max('h7), .width(4)) counter_2 (
    .up(1'b1), .count(y_inc), .clk(clk_t), .carry(counter_2_carry), .Q(pix_po));  // open: clr, load, D
  // Probe on x_t
  cursor_pos cursor_pos_1 (.x(register_1_q), .y(register_2_q), .dx(x_t), .dy(y_t));
  // Probe on y_t
  not not_1 (not_1_out, stopped);
  Register #(.width(1)) register_3 (.D(and_3_out), .en(not_1_out), .clk(clk_t), .Q(stopped), .clr(\continue ));
  and and_3 (and_3_out, y_inc, counter_2_carry);
  // Probe on pix_po
  Pull_Resistor pull_resistor_2 (.node(pix_po));
  Pull_Resistor pull_resistor_3 (.node(pull_resistor_3_node));
  Multiplexer #(.select(3)) multiplexer_1 (
    .in0(rom_data[4]), .in1(rom_data[3]), .in2(rom_data[2]), .in3(rom_data[1]), .in4(rom_data[0]),
    .in5(pull_resistor_3_node), .in6(pull_resistor_3_node), .in7(pull_resistor_3_node),
    .out(multiplexer_1_out), .sel(w_sel));
  assign WE = multiplexer_1_out ? 1'b1 : 1'bz;  // Controlled_Buffer controlled_buffer_1
  Pull_Resistor pull_resistor_4 (.node(WE));
  // Probe on dx
  Adder #(.width(7)) adder_1 (.a({4'b0000, w_sel}), .b(x_t), .out(dx));  // open: cin, cout
  // Probe on dy
  Adder #(.width(6)) adder_2 (.a({2'b00, pix_po}), .b(y_t), .out(dy));  // open: cin, cout

  // Other names for the same wires on the sheet: y_pos_tmp[3:0] = pix_po; halt = stopped; x_pos[6:0] = dx;
  //   y_pos[5:0] = dy
endmodule

module cursor_pos (
  input  [4:0] x,
  input  [2:0] y,
  output [6:0] dx,
  output [5:0] dy
);

  wire [2:0] pull_resistor_1_node;
  wire [4:0] pull_resistor_2_node;
  wire [7:0] multiplier_1_out;
  wire [7:6] multiplier_2_out;
  wire [7:7] adder_1_out;

  // Probe on x
  Pull_Resistor pull_resistor_1 (.node(pull_resistor_1_node));
  // Probe on y
  Pull_Resistor pull_resistor_2 (.node(pull_resistor_2_node));
  Multiplier multiplier_1 (.a({pull_resistor_1_node, x}), .b(8'h6), .out(multiplier_1_out));  // open: cin, cout
  Multiplier multiplier_2 (.a({pull_resistor_2_node, y}), .b(8'h9), .out({multiplier_2_out, dy}));  // open: cin, cout
  Adder adder_1 (.a(multiplier_1_out), .b(8'h1), .out({adder_1_out[7], dx}));  // open: cin, cout
  // Probe on {multiplier_2_out, dy}
  Pull_Resistor pull_resistor_3 (.node(dy));
  // Probe on {adder_1_out[7], dx}
  Pull_Resistor pull_resistor_4 (.node(dx));

  // Notes on the sheet:
  //   dy = 8y
  //   dx = 6x+1
endmodule
