// Logisim project cpu.circ as structural Verilog: 1 circuit, main circuit main
module main (
  input  in_1,
  input  [7:0] in_2,
  input  [1:0] in_3
);

  wire adder_1_cout, and_1_out, and_2_out, and_3_out, and_4_out, and_5_out, and_6_out, and_7_out, and_8_out,
       and_9_out, and_11_out, and_12_out, and_13_out, and_14_out, bcd_to_7_segment_decoder_2_p1,
       bcd_to_7_segment_decoder_3_p1, bcd_to_7_segment_decoder_6_p1, binary_to_bcd_converter_1_p2,
       binary_to_bcd_converter_2_p2, binary_to_bcd_converter_2_p4, buffer_4_out, busy_video, C_flag, CARRY,
       clock_1_out, cnue, comparator_1_eq, comparator_2_eq, comparator_3_eq, comparator_4_eq, dae,
       demultiplexer_2_out0, demultiplexer_2_out1, demultiplexer_2_out2, demultiplexer_2_out3,
       demultiplexer_2_out4, demultiplexer_6_out0, demultiplexer_6_out1, demultiplexer_6_out2,
       demultiplexer_6_out3, demultiplexer_6_out4, demultiplexer_8_out0, demultiplexer_8_out1,
       demultiplexer_8_out2, demultiplexer_8_out3, demultiplexer_8_out4, demultiplexer_9_out0,
       demultiplexer_9_out1, demultiplexer_9_out2, demultiplexer_9_out3, demultiplexer_9_out4,
       demultiplexer_10_out0, demultiplexer_10_out1, demultiplexer_10_out2, demultiplexer_10_out3,
       demultiplexer_10_out4, demultiplexer_11_out0, demultiplexer_11_out1, demultiplexer_11_out2,
       demultiplexer_11_out3, demultiplexer_11_out4, display, DIV, EI, EO, go_mov, INST_REG_READ,
       INST_REG_WRITE, inst_step, JUMP, lr_R, lr_W, mov, mov_tmp, MULT, NOP, not_2_out, not_4_out, not_5_out,
       not_6_out, not_7_out, NOT_SYS_CLK, op_t, or_1_out, or_2_out, PC_inc, PC_READ, PSR_REG_READ, PSR_WRITE,
       R0_R, R0_READ, R0_W, R0_WRITE, R1_R, R1_READ, R1_W, R1_WRITE, R2_R, R2_READ, R2_W, R2_WRITE, R3_R,
       R3_READ, R3_W, R3_WRITE, R4_R, R4_READ, R4_W, R4_WRITE, r_a, r_b, RAM_ADDR_WRITE, RAM_READ, RAM_WRITE,
       reg0_R, reg0_W, reg1_R, reg1_W, reg2_R, reg2_W, reg3_R, reg3_W, reg4_R, reg4_W, reg_sp_tmp_r,
       reg_sp_tmp_w, register_7_q, register_9_q, regs_sel, rgb_video_1_p3, sp_R, sp_reg_go_r, sp_reg_go_w,
       sp_reg_mgmt_r, sp_reg_mgmt_w, sp_W, stopped, SUB, SYS_CLK, U_DATA_WRITE, w_dst, xor_1_out, Z_flag;
  wire [0:0] and_10_out;
  wire [1:0] ALU_OP, flags;
  wire [2:0] counter_1_q, counter_2_q, counter_3_q, counter_4_q, y;
  wire [3:0] controlled_buffer_14_out, INST_STEP_COUNTER_q, pix_pos, READ_OP, reg_a, reg_b, reg_tmp,
       rgb_video_1_p6, WRITE_OP;
  wire [4:0] CGROM, controlled_buffer_17_out, INST_DECODE, x;
  wire [5:0] rgb_video_1_p5;
  wire [6:0] char, rgb_video_1_p4;
  wire [7:0] buffer_2_out, LR, OUT_DATA;
  wire [7:5] graphic_rom_1_rom_data;
  wire [10:0] dipswitch_1_sw11, INST_REG_q;
  wire [15:0] adder_1_out, ALU_IN_A, ALU_IN_B, bit_extender_1_out, buffer_1_out, buffer_3_out, divider_1_out,
       divider_1_rem, LR_q, MAIN_BUS, multiplier_1_cout, multiplier_1_out, R0_q, R1_q, R2_q, R3_q, R4_q,
       RAM_ADDR_q, RAM_MEM_dout, register_2_q, register_3_q, stack_alu_A, xor_4_out;
  wire [15:7] controlled_buffer_42_out;
  wire [15:8] controlled_buffer_65_out, register_1_q;

  Pull_Resistor pull_resistor_1 (.node(MAIN_BUS));
  Clock clock_1 (.out(clock_1_out));
  _7_Segment_Display u_7_segment_display_1 ();  // open: g, f, a, b, e, d, c, dp
  // BCD_to_7_Segment_decoder bcd_to_7_segment_decoder_1: pin names not known
  not not_1 (NOT_SYS_CLK, SYS_CLK);
  assign SYS_CLK = not_2_out ? clock_1_out : 1'bz;  // Controlled_Buffer controlled_buffer_1
  not not_2 (not_2_out, 1'b0);
  _7_Segment_Display u_7_segment_display_2 ();  // open: g, f, a, b, e, d, c, dp
  // BCD_to_7_Segment_decoder bcd_to_7_segment_decoder_2: pin names not known; wires that end beside it: bcd_to_7_segment_decoder_2_p1
  // Binary_to_BCD_converter #(.binvalue(8)) binary_to_bcd_converter_1: pin names not known; wires that end beside it: in_2, binary_to_bcd_converter_1_p2, binary_to_bcd_converter_1_p2, bcd_to_7_segment_decoder_2_p1
  Demultiplexer #(.select(4)) demultiplexer_1 (
    .out1(R0_READ), .out2(R1_READ), .out3(R2_READ), .out4(R3_READ), .out5(R4_READ), .out6(display),
    .out7(sp_R), .out8(lr_R), .out9(PSR_REG_READ), .out10(sp_reg_mgmt_w), .out11(mov), .out12(sp_reg_mgmt_r),
    .out13(INST_REG_READ), .out14(PC_READ), .out15(RAM_READ), .in(1'b1), .sel(READ_OP));  // open: out0
  // Probe on READ_OP
  Demultiplexer #(.select(4)) demultiplexer_2 (
    .out0(demultiplexer_2_out0), .out1(demultiplexer_2_out1), .out2(demultiplexer_2_out2),
    .out3(demultiplexer_2_out3), .out4(demultiplexer_2_out4), .in(1'b1), .sel(reg_tmp));  // open: out5, out6, out7, out8, out9, out10, out11, out12, out13, out14, out15
  // Probe on reg_tmp
  and and_1 (and_1_out, op_t, xor_1_out);
  xor xor_1 (xor_1_out, r_a, r_b);
  // Probe on MAIN_BUS
  // Probe on MAIN_BUS
  // Probe on in_2
  _7_Segment_Display u_7_segment_display_3 ();  // open: g, f, a, b, e, d, c, dp
  // BCD_to_7_Segment_decoder bcd_to_7_segment_decoder_3: pin names not known; wires that end beside it: bcd_to_7_segment_decoder_3_p1, bcd_to_7_segment_decoder_3_p1
  Counter #(.max('hf), .width(4)) INST_STEP_COUNTER (
    .clr(EI), .count(inst_step), .clk(NOT_SYS_CLK), .Q(INST_STEP_COUNTER_q));  // open: load, up, D, carry
  not not_3 (inst_step, busy_video);
  assign R1_R = and_1_out ? demultiplexer_2_out1 : 1'bz;  // Controlled_Buffer controlled_buffer_2
  assign R2_R = and_1_out ? demultiplexer_2_out2 : 1'bz;  // Controlled_Buffer controlled_buffer_3
  assign R3_R = and_1_out ? demultiplexer_2_out3 : 1'bz;  // Controlled_Buffer controlled_buffer_4
  xor xor_2 (reg0_R, R0_R, R0_READ);
  xor xor_3 (reg0_W, R0_W, R0_WRITE);
  Comparator #(.width(5)) comparator_1 (.a(INST_DECODE), .b(5'b01000), .eq(comparator_1_eq));  // open: gt, lt
  Comparator #(.width(5)) comparator_2 (.a(INST_DECODE), .b(5'b10011), .eq(comparator_2_eq));  // open: gt, lt
  assign R4_R = and_1_out ? demultiplexer_2_out4 : 1'bz;  // Controlled_Buffer controlled_buffer_5
  assign R0_R = and_1_out ? demultiplexer_2_out0 : 1'bz;  // Controlled_Buffer controlled_buffer_6
  Pull_Resistor pull_resistor_2 (.node(R0_R));
  Pull_Resistor pull_resistor_3 (.node(R1_R));
  Pull_Resistor pull_resistor_4 (.node(R2_R));
  Pull_Resistor pull_resistor_5 (.node(R3_R));
  Pull_Resistor pull_resistor_6 (.node(R4_R));
  // Probe on ALU_IN_A
  assign bit_extender_1_out = {{15{SUB}}, SUB};  // Bit_Extender bit_extender_1
  not not_4 (not_4_out, EO);
  assign CARRY = not_4_out ? 1'b0 : 1'bz;  // Controlled_Buffer controlled_buffer_7
  assign ALU_IN_A = comparator_1_eq ? stack_alu_A : 16'bz;  // Controlled_Buffer controlled_buffer_8
  assign ALU_IN_B = comparator_1_eq ? 16'h1 : 16'bz;  // Controlled_Buffer controlled_buffer_9
  assign ALU_IN_A = comparator_2_eq ? stack_alu_A : 16'bz;  // Controlled_Buffer controlled_buffer_10
  assign ALU_IN_B = comparator_2_eq ? {{12{1'b0}}, reg_a} : 16'bz;  // Controlled_Buffer controlled_buffer_11
  // Probe on ALU_IN_B
  assign xor_4_out = ALU_IN_B ^ bit_extender_1_out;  // XOR_Gate xor_4, 16 bits wide
  Multiplier #(.width(16)) multiplier_1 (
    .a(ALU_IN_A), .b(ALU_IN_B), .out(multiplier_1_out), .cout(multiplier_1_cout));  // open: cin
  or or_1 (or_1_out, multiplier_1_cout[15], multiplier_1_cout[14], multiplier_1_cout[13], multiplier_1_cout[12], multiplier_1_cout[11], multiplier_1_cout[10], multiplier_1_cout[9], multiplier_1_cout[8], multiplier_1_cout[7], multiplier_1_cout[6], multiplier_1_cout[5], multiplier_1_cout[4], multiplier_1_cout[3], multiplier_1_cout[2], multiplier_1_cout[1], multiplier_1_cout[0]);
  assign CARRY = and_3_out ? or_1_out : 1'bz;  // Controlled_Buffer controlled_buffer_12
  // Probe on flags
  xor xor_5 (reg1_R, R1_R, R1_READ);
  xor xor_6 (reg1_W, R1_W, R1_WRITE);
  Adder #(.width(16)) adder_1 (.a(ALU_IN_A), .b(xor_4_out), .out(adder_1_out), .cin(SUB), .cout(adder_1_cout));
  assign CARRY = and_2_out ? adder_1_cout : 1'bz;  // Controlled_Buffer controlled_buffer_13
  Pull_Resistor pull_resistor_7 (.node(ALU_IN_B));
  // Probe on INST_DECODE
  assign controlled_buffer_14_out = 1'b1 ? INST_STEP_COUNTER_q : 4'bz;  // Controlled_Buffer controlled_buffer_14
  not not_5 (not_5_out, 1'b1);
  DipSwitch #(.number(11)) dipswitch_1 (
    .sw1(dipswitch_1_sw11[10]), .sw2(dipswitch_1_sw11[9]), .sw3(dipswitch_1_sw11[8]),
    .sw4(dipswitch_1_sw11[7]), .sw5(dipswitch_1_sw11[6]), .sw6(dipswitch_1_sw11[5]),
    .sw7(dipswitch_1_sw11[4]), .sw8(dipswitch_1_sw11[3]), .sw9(dipswitch_1_sw11[2]),
    .sw10(dipswitch_1_sw11[1]), .sw11(dipswitch_1_sw11[0]));
  and and_2 (and_2_out, ~MULT, EO, ~DIV);  // AND_Gate
  assign MAIN_BUS = and_2_out ? adder_1_out : 16'bz;  // Controlled_Buffer controlled_buffer_15
  // Probe on adder_1_out
  and and_3 (and_3_out, MULT, EO, ~DIV);  // AND_Gate
  assign MAIN_BUS = and_3_out ? multiplier_1_out : 16'bz;  // Controlled_Buffer controlled_buffer_16
  // Probe on multiplier_1_out
  Pull_Resistor pull_resistor_8 (.node(ALU_IN_A));
  // Probe on controlled_buffer_14_out
  assign controlled_buffer_17_out = 1'b1 ? INST_DECODE : 5'bz;  // Controlled_Buffer controlled_buffer_17
  // Probe on {flags, controlled_buffer_17_out, controlled_buffer_14_out}
  ROM #(.addrWidth(11), .dataWidth(14)) ROM_MEM (
    .addr({flags, controlled_buffer_17_out, controlled_buffer_14_out}),
    .data({EO, PC_inc, NOP, EI, WRITE_OP, READ_OP, ALU_OP}));
  assign {flags, controlled_buffer_17_out, controlled_buffer_14_out} = not_5_out ? dipswitch_1_sw11 : 11'bz;  // Controlled_Buffer controlled_buffer_18
  // Probe on MAIN_BUS
  Counter #(.max('h4), .width(3)) counter_1 (
    .clr(EI), .up(1'b1), .count(1'b1), .clk(and_4_out), .Q(counter_1_q));  // open: load, D, carry
  and and_4 (and_4_out, op_t, SYS_CLK);
  Comparator #(.width(5)) comparator_3 (.a(INST_DECODE), .b(5'b00111), .eq(comparator_3_eq));  // open: gt, lt
  Comparator #(.width(5)) comparator_4 (.a(INST_DECODE), .b(5'b10100), .eq(comparator_4_eq));  // open: gt, lt
  _7_Segment_Display u_7_segment_display_4 ();  // open: g, f, a, b, e, d, c, dp
  // BCD_to_7_Segment_decoder bcd_to_7_segment_decoder_4: pin names not known
  // Binary_to_BCD_converter #(.binvalue(8)) binary_to_bcd_converter_2: pin names not known; wires that end beside it: OUT_DATA, binary_to_bcd_converter_2_p2, binary_to_bcd_converter_2_p2, binary_to_bcd_converter_2_p4
  // Probe on ALU_OP
  xor xor_7 (reg2_R, R2_R, R2_READ);
  xor xor_8 (reg2_W, R2_W, R2_WRITE);
  _7_Segment_Display u_7_segment_display_5 ();  // open: g, f, a, b, e, d, c, dp
  _7_Segment_Display u_7_segment_display_6 ();  // open: g, f, a, b, e, d, c, dp
  // BCD_to_7_Segment_decoder bcd_to_7_segment_decoder_5: pin names not known; wires that end beside it: binary_to_bcd_converter_2_p4
  // BCD_to_7_Segment_decoder bcd_to_7_segment_decoder_6: pin names not known; wires that end beside it: bcd_to_7_segment_decoder_6_p1, bcd_to_7_segment_decoder_6_p1
  Demultiplexer #(.select(2)) demultiplexer_3 (
    .out1(SUB), .out2(MULT), .out3(DIV), .in(1'b1), .sel(ALU_OP));  // open: out0
  Register #(.width(16)) register_1 (
    .D(MAIN_BUS), .en(regs_sel), .clk(SYS_CLK), .Q({register_1_q, reg_a, reg_b}));  // open: clr
  Divider #(.width(16)) divider_1 (
    .a(ALU_IN_A), .b(ALU_IN_B), .out(divider_1_out), .rem(divider_1_rem));  // open: upper
  or or_2 (or_2_out, divider_1_rem[15], divider_1_rem[14], divider_1_rem[13], divider_1_rem[12], divider_1_rem[11], divider_1_rem[10], divider_1_rem[9], divider_1_rem[8], divider_1_rem[7], divider_1_rem[6], divider_1_rem[5], divider_1_rem[4], divider_1_rem[3], divider_1_rem[2], divider_1_rem[1], divider_1_rem[0]);
  assign CARRY = and_5_out ? or_2_out : 1'bz;  // Controlled_Buffer controlled_buffer_19
  Register OUT_REG (.D(MAIN_BUS[7:0]), .en(U_DATA_WRITE), .clk(SYS_CLK), .Q(OUT_DATA));  // open: clr
  // Probe on {EO, PC_inc, NOP, EI, WRITE_OP, READ_OP, ALU_OP}
  // Probe on reg_a
  Demultiplexer #(.select(3)) demultiplexer_4 (
    .out2(r_b), .out3(r_a), .out4(w_dst), .in(1'b1), .sel(counter_1_q));  // open: out0, out1, out5, out6, out7
  assign ALU_IN_A = comparator_3_eq ? stack_alu_A : 16'bz;  // Controlled_Buffer controlled_buffer_20
  assign ALU_IN_B = comparator_3_eq ? 16'h1 : 16'bz;  // Controlled_Buffer controlled_buffer_21
  assign ALU_IN_A = comparator_4_eq ? stack_alu_A : 16'bz;  // Controlled_Buffer controlled_buffer_22
  assign ALU_IN_B = comparator_4_eq ? {{12{1'b0}}, reg_a} : 16'bz;  // Controlled_Buffer controlled_buffer_23
  and and_5 (and_5_out, ~MULT, EO, DIV);  // AND_Gate
  assign MAIN_BUS = and_5_out ? divider_1_out : 16'bz;  // Controlled_Buffer controlled_buffer_24
  // Probe on divider_1_out
  Demultiplexer #(.select(4)) demultiplexer_5 (
    .out1(R0_WRITE), .out2(R1_WRITE), .out3(R2_WRITE), .out4(R3_WRITE), .out5(R4_WRITE), .out6(cnue),
    .out7(sp_W), .out8(lr_W), .out9(JUMP), .out10(INST_REG_WRITE), .out11(RAM_WRITE), .out12(PSR_WRITE),
    .out13(RAM_ADDR_WRITE), .out14(U_DATA_WRITE), .out15(op_t), .in(1'b1), .sel(WRITE_OP));  // open: out0
  // Probe on WRITE_OP
  // Probe on reg_b
  xor xor_9 (reg3_R, R3_R, R3_READ);
  xor xor_10 (reg3_W, R3_W, R3_WRITE);
  Multiplexer #(.width(4)) multiplexer_1 (.in0(reg_a), .in1(reg_b), .out(reg_tmp), .sel(r_b));
  Demultiplexer #(.select(4)) demultiplexer_6 (
    .out0(demultiplexer_6_out0), .out1(demultiplexer_6_out1), .out2(demultiplexer_6_out2),
    .out3(demultiplexer_6_out3), .out4(demultiplexer_6_out4), .in(1'b1), .sel(reg_a));  // open: out5, out6, out7, out8, out9, out10, out11, out12, out13, out14, out15
  // Probe on reg_a
  // Probe on MAIN_BUS
  xor xor_11 (reg4_R, R4_R, R4_READ);
  xor xor_12 (reg4_W, R4_W, R4_WRITE);
  assign R0_W = w_dst ? demultiplexer_6_out0 : 1'bz;  // Controlled_Buffer controlled_buffer_25
  assign R1_W = w_dst ? demultiplexer_6_out1 : 1'bz;  // Controlled_Buffer controlled_buffer_26
  assign R2_W = w_dst ? demultiplexer_6_out2 : 1'bz;  // Controlled_Buffer controlled_buffer_27
  assign R3_W = w_dst ? demultiplexer_6_out3 : 1'bz;  // Controlled_Buffer controlled_buffer_28
  Pull_Resistor pull_resistor_9 (.node(R0_W));
  and and_6 (and_6_out, op_t, INST_REG_READ);
  and and_7 (and_7_out, mov_tmp, INST_REG_READ);
  and and_8 (and_8_out, reg_sp_tmp_r, INST_REG_READ);
  and and_9 (and_9_out, reg_sp_tmp_w, INST_REG_READ);
  Register #(.width(16)) R0 (.D(MAIN_BUS), .en(reg0_W), .clk(SYS_CLK), .Q(R0_q));  // open: clr
  Register #(.width(16)) R1 (.D(MAIN_BUS), .en(reg1_W), .clk(SYS_CLK), .Q(R1_q));  // open: clr
  Register #(.width(16)) R2 (.D(MAIN_BUS), .en(reg2_W), .clk(SYS_CLK), .Q(R2_q));  // open: clr
  Register #(.width(16)) R3 (.D(MAIN_BUS), .en(reg3_W), .clk(SYS_CLK), .Q(R3_q));  // open: clr
  Register #(.width(16)) R4 (.D(MAIN_BUS), .en(reg4_W), .clk(SYS_CLK), .Q(R4_q));  // open: clr
  Register #(.width(1)) tmp_reg (.D(PSR_REG_READ), .en(PSR_REG_READ), .clk(SYS_CLK), .Q(dae), .clr(EI));
  assign R4_W = w_dst ? demultiplexer_6_out4 : 1'bz;  // Controlled_Buffer controlled_buffer_29
  Pull_Resistor pull_resistor_10 (.node(R1_W));
  Pull_Resistor pull_resistor_11 (.node(R2_W));
  Pull_Resistor pull_resistor_12 (.node(R3_W));
  Pull_Resistor pull_resistor_13 (.node(R4_W));
  assign MAIN_BUS = reg0_R ? R0_q : 16'bz;  // Controlled_Buffer controlled_buffer_30
  assign MAIN_BUS = reg1_R ? R1_q : 16'bz;  // Controlled_Buffer controlled_buffer_31
  assign MAIN_BUS = reg2_R ? R2_q : 16'bz;  // Controlled_Buffer controlled_buffer_32
  assign MAIN_BUS = reg3_R ? R3_q : 16'bz;  // Controlled_Buffer controlled_buffer_33
  assign MAIN_BUS = reg4_R ? R4_q : 16'bz;  // Controlled_Buffer controlled_buffer_34
  // Probe on MAIN_BUS
  // Probe on MAIN_BUS[7:0]
  ExactlyOne xor_13 (.out(regs_sel), .in0(and_6_out), .in1(and_7_out), .in2(and_8_out), .in3(and_9_out));
  Counter PC (.load(JUMP), .count(PC_inc), .clk(SYS_CLK), .D(MAIN_BUS[7:0]), .Q(LR));  // open: clr, up, carry
  Register #(.width(16)) RAM_ADDR (.D(MAIN_BUS), .en(RAM_ADDR_WRITE), .clk(SYS_CLK), .Q(RAM_ADDR_q));  // open: clr
  // Probe on {{8{1'b0}}, LR}
  assign buffer_1_out = MAIN_BUS;  // Buffer buffer_1, 16 bits wide
  Register #(.width(16)) register_2 (.D(MAIN_BUS), .en(r_a), .clk(SYS_CLK), .Q(register_2_q));  // open: clr
  Register #(.width(16)) register_3 (.D(MAIN_BUS), .en(r_b), .clk(SYS_CLK), .Q(register_3_q));  // open: clr
  Register #(.width(1)) register_4 (.D(not_6_out), .en(mov), .clk(SYS_CLK), .Q(mov_tmp), .clr(go_mov));
  Register #(.width(1)) register_5 (.D(1'b1), .en(sp_reg_mgmt_r), .clk(SYS_CLK), .Q(reg_sp_tmp_r), .clr(EI));
  Register #(.width(1)) register_6 (.D(1'b1), .en(sp_reg_mgmt_w), .clk(SYS_CLK), .Q(reg_sp_tmp_w), .clr(EI));
  // Probe on MAIN_BUS
  and and_10 (and_10_out[0], ~buffer_1_out[15], ~buffer_1_out[14], ~buffer_1_out[13], ~buffer_1_out[12], ~buffer_1_out[11], ~buffer_1_out[10], ~buffer_1_out[9], ~buffer_1_out[8], ~buffer_1_out[7], ~buffer_1_out[6], ~buffer_1_out[5], ~buffer_1_out[4], ~buffer_1_out[3], ~buffer_1_out[2], ~buffer_1_out[1], ~buffer_1_out[0]);  // AND_Gate
  assign buffer_2_out = {8{1'b0}};  // Buffer buffer_2, 8 bits wide
  // Probe on {buffer_2_out, LR}
  assign ALU_IN_A = op_t ? register_2_q : 16'bz;  // Controlled_Buffer controlled_buffer_35
  assign ALU_IN_B = op_t ? register_3_q : 16'bz;  // Controlled_Buffer controlled_buffer_36
  not not_6 (not_6_out, go_mov);
  Register #(.width(2)) PSR_REG (
    .D({CARRY, and_10_out[0]}), .en(PSR_WRITE), .clk(SYS_CLK), .Q({C_flag, Z_flag}));  // open: clr
  Register #(.width(16)) SP (.D(MAIN_BUS), .en(sp_W), .clk(SYS_CLK), .Q(stack_alu_A));  // open: clr
  Register #(.width(16)) u_LR (.D({{8{1'b0}}, LR}), .en(lr_W), .clk(SYS_CLK), .Q(LR_q));  // open: clr
  assign MAIN_BUS = PC_READ ? {buffer_2_out, LR} : 16'bz;  // Controlled_Buffer controlled_buffer_37
  Register #(.width(16)) INST_REG (
    .D(MAIN_BUS), .en(INST_REG_WRITE), .clk(SYS_CLK), .Q({INST_DECODE, INST_REG_q}), .clr(EI));
  assign MAIN_BUS = sp_R ? stack_alu_A : 16'bz;  // Controlled_Buffer controlled_buffer_38
  assign MAIN_BUS = lr_R ? LR_q : 16'bz;  // Controlled_Buffer controlled_buffer_39
  RAM #(.addrWidth(16), .asyncread("true"), .dataWidth(16), .\type ("nonvolatile")) RAM_MEM (
    .addr(buffer_3_out), .we(buffer_4_out), .clk(SYS_CLK), .din(MAIN_BUS), .dout(RAM_MEM_dout));  // open: oe
  assign buffer_3_out = RAM_ADDR_q;  // Buffer buffer_3, 16 bits wide
  buf buffer_4 (buffer_4_out, RAM_WRITE);
  // Probe on {INST_DECODE, INST_REG_q}
  and and_11 (and_11_out, reg_sp_tmp_w, SYS_CLK);
  Register #(.width(1)) register_7 (.D(display), .en(display), .clk(SYS_CLK), .Q(register_7_q), .clr(stopped));
  and and_12 (and_12_out, ~INST_REG_WRITE, INST_REG_READ);  // AND_Gate
  assign MAIN_BUS = and_12_out ? {{5{1'b0}}, INST_REG_q} : 16'bz;  // Controlled_Buffer controlled_buffer_40
  // Probe on INST_DECODE
  assign flags = not_7_out ? in_3 : 2'bz;  // Controlled_Buffer controlled_buffer_41
  Counter #(.max('h4), .width(3)) counter_2 (
    .clr(EI), .up(1'b1), .count(1'b1), .clk(and_11_out), .Q(counter_2_q));  // open: load, D, carry
  assign {controlled_buffer_42_out, char} = register_7_q ? MAIN_BUS : 16'bz;  // Controlled_Buffer controlled_buffer_42
  Register #(.width(1)) register_8 (.D(register_7_q), .en(register_7_q), .clk(SYS_CLK), .Q(busy_video), .clr(stopped));
  assign flags = dae ? {C_flag, Z_flag} : 2'bz;  // Controlled_Buffer controlled_buffer_43
  not not_7 (not_7_out, dae);
  Pull_Resistor pull_resistor_14 (.node({controlled_buffer_42_out, char}));
  // Probe on char
  assign MAIN_BUS = RAM_READ ? RAM_MEM_dout : 16'bz;  // Controlled_Buffer controlled_buffer_44
  // Probe on RAM_MEM_dout
  Demultiplexer #(.select(3)) demultiplexer_7 (
    .out4(sp_reg_go_w), .in(1'b1), .sel(counter_2_q));  // open: out0, out1, out2, out3, out5, out6, out7
  Demultiplexer #(.select(4)) demultiplexer_8 (
    .out0(demultiplexer_8_out0), .out1(demultiplexer_8_out1), .out2(demultiplexer_8_out2),
    .out3(demultiplexer_8_out3), .out4(demultiplexer_8_out4), .in(1'b1), .sel(reg_b));  // open: out5, out6, out7, out8, out9, out10, out11, out12, out13, out14, out15
  // Probe on reg_b
  Demultiplexer #(.select(4)) demultiplexer_9 (
    .out0(demultiplexer_9_out0), .out1(demultiplexer_9_out1), .out2(demultiplexer_9_out2),
    .out3(demultiplexer_9_out3), .out4(demultiplexer_9_out4), .in(1'b1), .sel(reg_a));  // open: out5, out6, out7, out8, out9, out10, out11, out12, out13, out14, out15
  // Probe on reg_a
  and and_13 (and_13_out, mov_tmp, SYS_CLK);
  Demultiplexer #(.select(4)) demultiplexer_10 (
    .out0(demultiplexer_10_out0), .out1(demultiplexer_10_out1), .out2(demultiplexer_10_out2),
    .out3(demultiplexer_10_out3), .out4(demultiplexer_10_out4), .in(1'b1), .sel(reg_b));  // open: out5, out6, out7, out8, out9, out10, out11, out12, out13, out14, out15
  // Probe on reg_b
  Demultiplexer #(.select(4)) demultiplexer_11 (
    .out0(demultiplexer_11_out0), .out1(demultiplexer_11_out1), .out2(demultiplexer_11_out2),
    .out3(demultiplexer_11_out3), .out4(demultiplexer_11_out4), .in(1'b1), .sel(reg_b));  // open: out5, out6, out7, out8, out9, out10, out11, out12, out13, out14, out15
  // Probe on reg_b
  assign R3_R = go_mov ? demultiplexer_8_out3 : 1'bz;  // Controlled_Buffer controlled_buffer_45
  assign R2_W = go_mov ? demultiplexer_9_out2 : 1'bz;  // Controlled_Buffer controlled_buffer_46
  assign R3_W = go_mov ? demultiplexer_9_out3 : 1'bz;  // Controlled_Buffer controlled_buffer_47
  Counter #(.max('h4), .width(3)) counter_3 (
    .clr(EI), .up(1'b1), .count(1'b1), .clk(and_13_out), .Q(counter_3_q));  // open: load, D, carry
  assign R2_R = sp_reg_go_r ? demultiplexer_10_out2 : 1'bz;  // Controlled_Buffer controlled_buffer_48
  assign R3_R = sp_reg_go_r ? demultiplexer_10_out3 : 1'bz;  // Controlled_Buffer controlled_buffer_49
  Counter #(.max('h4), .width(3)) counter_4 (
    .clr(EI), .up(1'b1), .count(1'b1), .clk(and_14_out), .Q(counter_4_q));  // open: load, D, carry
  and and_14 (and_14_out, reg_sp_tmp_r, SYS_CLK);
  assign R0_R = go_mov ? demultiplexer_8_out0 : 1'bz;  // Controlled_Buffer controlled_buffer_50
  assign R1_R = go_mov ? demultiplexer_8_out1 : 1'bz;  // Controlled_Buffer controlled_buffer_51
  assign R2_R = go_mov ? demultiplexer_8_out2 : 1'bz;  // Controlled_Buffer controlled_buffer_52
  Pull_Resistor pull_resistor_15 (.node(R0_R));
  Pull_Resistor pull_resistor_16 (.node(R1_R));
  Pull_Resistor pull_resistor_17 (.node(R2_R));
  assign R0_W = go_mov ? demultiplexer_9_out0 : 1'bz;  // Controlled_Buffer controlled_buffer_53
  assign R1_W = go_mov ? demultiplexer_9_out1 : 1'bz;  // Controlled_Buffer controlled_buffer_54
  Pull_Resistor pull_resistor_18 (.node(R0_W));
  Pull_Resistor pull_resistor_19 (.node(R1_W));
  Pull_Resistor pull_resistor_20 (.node(R2_W));
  Pull_Resistor pull_resistor_21 (.node(R3_W));
  assign R0_R = sp_reg_go_r ? demultiplexer_10_out0 : 1'bz;  // Controlled_Buffer controlled_buffer_55
  assign R1_R = sp_reg_go_r ? demultiplexer_10_out1 : 1'bz;  // Controlled_Buffer controlled_buffer_56
  Pull_Resistor pull_resistor_22 (.node(R0_R));
  Pull_Resistor pull_resistor_23 (.node(R1_R));
  Pull_Resistor pull_resistor_24 (.node(R2_R));
  Pull_Resistor pull_resistor_25 (.node(R3_R));
  assign R0_W = sp_reg_go_w ? demultiplexer_11_out0 : 1'bz;  // Controlled_Buffer controlled_buffer_57
  assign R1_W = sp_reg_go_w ? demultiplexer_11_out1 : 1'bz;  // Controlled_Buffer controlled_buffer_58
  assign R2_W = sp_reg_go_w ? demultiplexer_11_out2 : 1'bz;  // Controlled_Buffer controlled_buffer_59
  assign R3_W = sp_reg_go_w ? demultiplexer_11_out3 : 1'bz;  // Controlled_Buffer controlled_buffer_60
  Pull_Resistor pull_resistor_26 (.node(R0_W));
  assign R4_R = go_mov ? demultiplexer_8_out4 : 1'bz;  // Controlled_Buffer controlled_buffer_61
  Pull_Resistor pull_resistor_27 (.node(R3_R));
  Pull_Resistor pull_resistor_28 (.node(R4_R));
  assign R4_W = go_mov ? demultiplexer_9_out4 : 1'bz;  // Controlled_Buffer controlled_buffer_62
  Pull_Resistor pull_resistor_29 (.node(R4_W));
  assign R4_R = sp_reg_go_r ? demultiplexer_10_out4 : 1'bz;  // Controlled_Buffer controlled_buffer_63
  Pull_Resistor pull_resistor_30 (.node(R4_R));
  assign R4_W = sp_reg_go_w ? demultiplexer_11_out4 : 1'bz;  // Controlled_Buffer controlled_buffer_64
  Pull_Resistor pull_resistor_31 (.node(R1_W));
  Pull_Resistor pull_resistor_32 (.node(R2_W));
  Pull_Resistor pull_resistor_33 (.node(R3_W));
  Pull_Resistor pull_resistor_34 (.node(R4_W));
  Demultiplexer #(.select(3)) demultiplexer_12 (
    .out3(go_mov), .in(1'b1), .sel(counter_3_q));  // open: out0, out1, out2, out4, out5, out6, out7
  Demultiplexer #(.select(3)) demultiplexer_13 (
    .out4(sp_reg_go_r), .in(1'b1), .sel(counter_4_q));  // open: out0, out1, out2, out3, out5, out6, out7
  // Probe on CGROM
  assign {controlled_buffer_65_out, x, y} = cnue ? MAIN_BUS : 16'bz;  // Controlled_Buffer controlled_buffer_65
  Graphic_ROM graphic_rom_1 (.char_pix_pos(pix_pos), .char_code(char), .ROM_data({graphic_rom_1_rom_data, CGROM}));
  // Probe on y
  // Probe on x
  Pull_Resistor pull_resistor_35 (.node({controlled_buffer_65_out, x, y}));
  // RGB_Video #(.height(64)) rgb_video_1: pin names not known; wires that end beside it: in_1, SYS_CLK, rgb_video_1_p3, rgb_video_1_p4, rgb_video_1_p5, rgb_video_1_p6
  Graphic_ctrl graphic_ctrl_1 (
    .rom_data(CGROM), .x(x), .y(y), .EN(busy_video), .clk(SYS_CLK), .cursor(register_9_q), .\continue (cnue),
    .WE(rgb_video_1_p3), .dy(rgb_video_1_p5), .dx(rgb_video_1_p4), .color(rgb_video_1_p6), .stopped(stopped),
    .pix_po(pix_pos));
  // Probe on rgb_video_1_p4
  // Probe on rgb_video_1_p5
  Register #(.width(1)) register_9 (.D(cnue), .en(1'b1), .clk(SYS_CLK), .Q(register_9_q));  // open: clr
  // Probe on stopped

  // Other names for the same wires on the sheet: PC[7:0] = LR; disp_EN = busy_video; OUT_ALU[15:0] = MAIN_BUS;
  //   set_cursor = cnue; U_DATA[7:0] = in_2

  // Notes on the sheet:
  //   Pull bus down, prevent undefined state
  //   Input from the user
  //   Decode the input 8 bits (0-255)
  //   PEEK
  //   SMTH
  //   POP
  //   READ operations
  //   only required in addition mode
  //   Addition/substraction
  //   Manual mode bit 0
  //   Carry bit is 0 at the begining, if execution ends,
  //    carry equals the carry out of the operation executed
  //   Multiplication
  //   Instruction counter
  //   Manual input test
  //   ALU
  //   contents of ROM_MEM (hex, n*v repeats v):
  //   378 12bc 16*0 374 7c 400 13*0 374 bc 400 13*0 374 fc 400 13*0 374 13c 400 13*0 374 17c 400 13*0 374
  //   18 3c 400 12*0 30 34 35c 2c0 2c0 1c 21c1 400 8*0 1c 21c0 28 34 35c 3c 3c 400 8*0 3f4 3c0 3c0 3c0
  //   23c0 400 10*0 3f4 3c0 3c0 3c0 23c1 400 10*0 3f4 3c0 3c0 3c0 23c2 400 10*0 3f4 3c0 3c0 3c0 23c3 400
  //   10*0 374 2c4 400 13*0 374 2c8 400 13*0 347 2cc 400 13*0 374 2d0 400 13*0 374 2d4 400 13*0 1b4 400
  //   14*0 28 34 2340 3c 3c 400 10*0 30 34 2340 2c0 2c0 400 9*0 34 274 400 13*0 34 24 400 13*0 34 24 400
  //   13*0 34 74 400 13*0 34 b4 400 14*0 374 3bc 400 13*0 2c 34 2c 2c 400 11*0 34 1f4 400 13*0 20 260 400
  //   13*0 200 34 274 400 12*0 800 400 367*0 400 15*0 274 400 494*0 274 400 14*0 400 495*0 274 400 14*0
  //   274 400
  //   PUSH
  //   POKE
  //   DECODER
  //   Decode the output 8 bits (0-255)
  //   Selection of the ALU operation here
  //   Division
  //   ALU operations
  //   DISP
  //   [13]
  //   WRITE operations
  //   [0-1]
  //   [10]
  //   [11]
  //   [2-5]
  //   [6-9]
  //   [12]
  //   Set the counter to a desired address
  //   Execution: PC point to the address in memory
  //   00000 (inst)
  //   Which is the address selection input, data at this location is then writen in main_bus
  //   This data is the input of the instruction register, it then split into operation and address
  //   The operation gets decrypted from ROM and set the related bits of the operation high
  //   00000000000 (addr)
  //   PC & RAM
  //   Should not R and W at the same time
  //   REGISTER BANK
  //   Split, Read the instruction and forward it back
endmodule
